# Fritzing sketch Boatsensor_v2.0 (saved by Fritzing 0.9.10b)
breadboards: 1

parts:
  Part1 = Arduino Uno (Rev3)
  U1 = 74HC595 [package="DIP16 [THT]"]
  R1 = Resistor [tolerance=±5% power=0.25 resistance=220 package=THT]
  R2 = Resistor [tolerance=±5% power=0.25 resistance=220 package=THT]
  R3 = Resistor [tolerance=±5% power=0.25 resistance=220 package=THT]
  R4 = Resistor [tolerance=±5% power=0.25 resistance=220 package=THT]
  R5 = Resistor [tolerance=±5% power=0.25 resistance=220 package=THT]
  R6 = Resistor [tolerance=±5% power=0.25 resistance=220 package=THT]
  R7 = Resistor [tolerance=±5% power=0.25 resistance=220 package=THT]
  R8 = Resistor [tolerance=±5% power=0.25 resistance=220 package=THT]
  LED1 = 7-SEGMENT-4DIGIT-YOUNGSUN [package=7-segment-4digit-youngsun]
  Q1 = NPN-Transistor [package="SOT-23 [SMD]"]
  Q2 = NPN-Transistor [package="SOT-23 [SMD]"]
  Q3 = NPN-Transistor [package="SOT-23 [SMD]"]
  Q4 = NPN-Transistor [package="SOT-23 [SMD]"]
  LED2 = LED - 3mm [color="Red (633nm)" current=0.030 package="3 mm [THT]"]
  R9 = Resistor [tolerance=±5% power=0.25 resistance=220 package=THT]
  R10 = Resistor [tolerance=±5% power=0.25 resistance=220 package=THT]
  LED3 = LED - 3mm [color="Green (555nm)" current=30mA package="3 mm [THT]"]
  R11 = PHOTOCELL [package=photocell]
  R13 = Resistor [tolerance=±5% power=0.25 resistance=10k package=THT]
  Mod1 = Amica NodeMCU DEVKIT 1.0
  HC-SR04_Sensor_1 = HC-SR04 Ultrasonic Distance Sensor
  U2 = RF-LINK_TX [package=rf-link_tx]

nets:
  N1: Part1.A0, R11.P$2, R13.Pin_0
  N2: Part1.D9_PWM, LED3.anode
  N3: Part1.D10_PWM/SS, U1.SH_CP
  N4: Part1.D11_PWM/MOSI, U1.ST_CP
  N5: Part1.D12/MISO, U1.DS
  GND: Part1.GND, Part1.D0/RX, U1.GND, U1.OE, Q1.1, Q2.1, Q3.1, Q4.1, R9.Pin_0, R10.Pin_0, R13.Pin_1, Mod1.pin2, Mod1.pin3, Mod1.pin_9, Mod1.pin_25, Mod1.pin_29, HC-SR04_Sensor_1.GND, U2.GND
  N6: Part1.D1/TX, Mod1.pin4
  N7: Part1.D3_PWM, LED2.anode
  N8: Part1.D4, Q4.0
  N9: Part1.D5_PWM, Q3.0
  N10: Part1.D6_PWM, Q2.0
  N11: Part1.D7, Q1.0
  VCC: Part1.5V, U1.MR, U1.VCC, R11.P$1, Mod1.pin1, Mod1.pin_10, Mod1.pin_26, Mod1.pin_27, HC-SR04_Sensor_1.VCC, U2.ANT
  N12: U1.Q1, R2.Pin_1
  N13: U1.Q2, R3.Pin_1
  N14: U1.Q3, R4.Pin_1
  N15: U1.Q4, R5.Pin_1
  N16: U1.Q5, R6.Pin_1
  N17: U1.Q6, R7.Pin_1
  N18: U1.Q7, R8.Pin_1
  N19: U1.Q0, R1.Pin_1
  N20: R1.Pin_0, LED1.G
  N21: R2.Pin_0, LED1.A
  N22: R3.Pin_0, LED1.F
  N23: R4.Pin_0, LED1.DIG1
  N24: R5.Pin_0, LED1.DIG2
  N25: R6.Pin_0, LED1.D
  N26: R7.Pin_0, LED1.COL-A
  N27: LED1.DIG3, Q1.2
  N28: LED1.COL-C, Q2.2
  N29: LED1.C, Q3.2
  N30: LED1.B, Q4.2
  N31: LED2.cathode, R9.Pin_1
  N32: R10.Pin_1, LED3.cathode
  N33: Mod1.pin_11, Mod1.pin_12, U2.DATA
  N34: Mod1.pin_13, U2.+5V
  N35: Mod1.pin_14, HC-SR04_Sensor_1.TRIG
  N36: Mod1.pin_15, HC-SR04_Sensor_1.ECHO
